# Fritzing sketch rx (saved by Fritzing 0.9.2b)
circuit board: 8.46667cm x 5.64444cm
breadboards: 1

parts:
  IC1 = MICROCONTROLLER [package=dil28-3-simon-kit]
  R1 = Resistor [tolerance=±5% resistance=10k package=THT]
  CR2032 = Battery Holders [package=battcon_245mm_pth]
  CR2032_2 = Battery Holders [package=battcon_245mm_pth]
  C1_4_7nF = Tantalum Capacitor [capacitance=1μF package="100 mil [THT, tantalum]"]
  C3 = Tantalum Capacitor [capacitance=1μF package="100 mil [THT, tantalum]"]
  S1 = Momentary Switch [package=ksa_sealed_tac_switch]
  R2 = Resistor [tolerance=±10% resistance=330 package=THT]
  C4_100nF = Tantalum Capacitor [capacitance=1μF package="100 mil [THT, tantalum]"]
  C5_100nF = Tantalum Capacitor [capacitance=1μF package="100 mil [THT, tantalum]"]
  C6_100nF = Tantalum Capacitor [capacitance=1μF package="100 mil [THT, tantalum]"]
  MOSI_MISO = female pin header, 2 pins [form="♀ (female)"]
  SCK_RESET = female pin header, 2 pins [form="♀ (female)"]
  VCC_GND = female pin header, 2 pins [form="♀ (female)"]
  LED1 = LED - 3mm [color="Red (633nm)" package="3 mm [THT]"]
  C2 = Tantalum Capacitor [capacitance=1μF package="100 mil [THT, tantalum]"]
  D1 = Rectifier Diode [part_number=UF4001 package="300 mil [THT]"]
  U2 = RF-LINK_RX [package=rf-link_rx]

nets:
  N1: IC1.PC6(_RESET), R1.Pin_1, C1_4_7nF.+, R2.Pin_1, SCK_RESET.pin2
  VCC: IC1.VCC, C6_100nF.+, VCC_GND.pin1, U2.+5V
  GND: IC1.GND, IC1.AGND, C1_4_7nF.-, C4_100nF.-, C5_100nF.-, C6_100nF.-, VCC_GND.pin2, LED1.cathode, U2.GND
  N2: IC1.PB3(MOSI_OC2), MOSI_MISO.pin1
  N3: IC1.PB4(MISO), MOSI_MISO.pin2, U2.DATA
  N4: IC1.PB5(SCK), SCK_RESET.pin1
  N5: IC1.AVCC, C5_100nF.+
  N6: IC1.AREF, C4_100nF.+
  N7: IC1.PC0(ADC0), LED1.anode
  N8: CR2032.+, C2.+
  N9: CR2032_2.-, C3.-, S1.1
  N10: C3.+, C2.-, D1.cathode
